// Logisim project ADD.circ as structural Verilog: 1 circuit, main circuit sumador
module sumador (
  input  [15:0] A,
  input  [15:0] B,
  output [15:0] Result,
  output out_4
);

  wire and_1_out, and_2_out, and_3_out, and_4_out, and_5_out, and_6_out, and_7_out, and_8_out, and_9_out,
       and_10_out, and_11_out, and_12_out, and_13_out, and_14_out, and_15_out, and_16_out, and_17_out,
       and_18_out, and_19_out, and_20_out, and_21_out, and_22_out, and_23_out, and_24_out, and_25_out,
       and_26_out, and_27_out, and_28_out, and_29_out, and_30_out, and_31_out, and_32_out, C_2_out, C_3_out,
       C_4_out, C_5_out, C_6_out, C_7_out, C_8_out, C_9_out, C_10_out, C_11_out, C_12_out, C_13_out,
       C_15_out, C_16_out, C_out, xor_1_out, xor_2_out, xor_3_out, xor_4_out, xor_5_out, xor_6_out,
       xor_7_out, xor_8_out, xor_9_out, xor_10_out, xor_11_out, xor_12_out, xor_13_out, xor_14_out,
       xor_15_out, xor_16_out;

  and and_1 (and_1_out, A[0], B[0]);
  and and_2 (and_2_out, A[1], B[1]);
  and and_3 (and_3_out, A[2], B[2]);
  and and_4 (and_4_out, A[4], B[4]);
  and and_5 (and_5_out, A[5], B[5]);
  and and_6 (and_6_out, A[7], B[7]);
  and and_7 (and_7_out, A[8], B[8]);
  and and_8 (and_8_out, A[9], B[9]);
  and and_9 (and_9_out, A[10], B[10]);
  and and_10 (and_10_out, A[11], B[11]);
  and and_11 (and_11_out, A[12], B[12]);
  and and_12 (and_12_out, A[13], B[13]);
  and and_13 (and_13_out, A[14], B[14]);
  and and_14 (and_14_out, A[15], B[15]);
  xor xor_1 (xor_1_out, A[0], B[0]);
  xor xor_2 (xor_2_out, A[1], B[1]);
  xor xor_3 (xor_3_out, A[2], B[2]);
  xor xor_4 (xor_4_out, A[3], B[3]);
  and and_15 (and_15_out, A[3], B[3]);
  xor xor_5 (xor_5_out, A[4], B[4]);
  xor xor_6 (xor_6_out, A[5], B[5]);
  xor xor_7 (xor_7_out, A[6], B[6]);
  and and_16 (and_16_out, A[6], B[6]);
  xor xor_8 (xor_8_out, A[7], B[7]);
  xor xor_9 (xor_9_out, A[8], B[8]);
  xor xor_10 (xor_10_out, A[9], B[9]);
  xor xor_11 (xor_11_out, A[10], B[10]);
  xor xor_12 (xor_12_out, A[11], B[11]);
  xor xor_13 (xor_13_out, A[12], B[12]);
  xor xor_14 (xor_14_out, A[13], B[13]);
  xor xor_15 (xor_15_out, A[14], B[14]);
  xor xor_16 (xor_16_out, A[15], B[15]);
  xor xor_17 (Result[0], xor_1_out, 1'b0);
  or C (C_out, and_17_out, and_1_out);
  and and_17 (and_17_out, xor_1_out, 1'b0);
  xor xor_18 (Result[1], xor_2_out, C_out);
  or C_2 (C_2_out, and_18_out, and_2_out);
  and and_18 (and_18_out, xor_2_out, C_out);
  xor xor_19 (Result[2], xor_3_out, C_2_out);
  or C_3 (C_3_out, and_19_out, and_3_out);
  and and_19 (and_19_out, xor_3_out, C_2_out);
  xor xor_20 (Result[3], xor_4_out, C_3_out);
  and and_20 (and_20_out, xor_4_out, C_3_out);
  xor xor_21 (Result[4], xor_5_out, C_15_out);
  or C_4 (C_4_out, and_21_out, and_4_out);
  and and_21 (and_21_out, xor_5_out, C_15_out);
  xor xor_22 (Result[5], xor_6_out, C_4_out);
  and and_22 (and_22_out, xor_6_out, C_4_out);
  or C_5 (C_5_out, and_22_out, and_5_out);
  xor xor_23 (Result[6], xor_7_out, C_5_out);
  and and_23 (and_23_out, xor_7_out, C_5_out);
  xor xor_24 (Result[7], xor_8_out, C_16_out);
  and and_24 (and_24_out, xor_8_out, C_16_out);
  or C_6 (C_6_out, and_24_out, and_6_out);
  xor xor_25 (Result[8], xor_9_out, C_6_out);
  or C_7 (C_7_out, and_25_out, and_7_out);
  and and_25 (and_25_out, xor_9_out, C_6_out);
  xor xor_26 (Result[9], xor_10_out, C_7_out);
  and and_26 (and_26_out, xor_10_out, C_7_out);
  or C_8 (C_8_out, and_26_out, and_8_out);
  xor xor_27 (Result[10], xor_11_out, C_8_out);
  and and_27 (and_27_out, xor_11_out, C_8_out);
  or C_9 (C_9_out, and_27_out, and_9_out);
  xor xor_28 (Result[11], xor_12_out, C_9_out);
  and and_28 (and_28_out, xor_12_out, C_9_out);
  or C_10 (C_10_out, and_28_out, and_10_out);
  xor xor_29 (Result[12], xor_13_out, C_10_out);
  or C_11 (C_11_out, and_29_out, and_11_out);
  and and_29 (and_29_out, xor_13_out, C_10_out);
  xor xor_30 (Result[13], xor_14_out, C_11_out);
  or C_12 (C_12_out, and_30_out, and_12_out);
  and and_30 (and_30_out, xor_14_out, C_11_out);
  xor xor_31 (Result[14], xor_15_out, C_12_out);
  or C_13 (C_13_out, and_31_out, and_13_out);
  and and_31 (and_31_out, xor_15_out, C_12_out);
  xor xor_32 (Result[15], xor_16_out, C_13_out);
  and and_32 (and_32_out, xor_16_out, C_13_out);
  or C_14 (out_4, and_32_out, and_14_out);
  or C_15 (C_15_out, and_20_out, and_15_out);
  or C_16 (C_16_out, and_23_out, and_16_out);
endmodule
