// Logisim project ALU.circ as structural Verilog: 1 circuit, main circuit main
module main (
  input  [3:0] NEM,
  input  [15:0] RS1,
  input  [15:0] RS2,
  output [15:0] Resultado,
  output Bbit
);

  wire demultiplexer_1_out0, demultiplexer_1_out1, demultiplexer_1_out2, demultiplexer_1_out3,
       demultiplexer_1_out4, demultiplexer_1_out5, demultiplexer_1_out6, demultiplexer_1_out7, main_6_bbit,
       main_7_branchbit;
  wire [15:0] main_1_out_3, main_2_re, main_3_re, main_4_result, main_5_result, sumador_1_p3;

  // sumador sumador_1: pin names not known; wires that end beside it: RS1, RS2, sumador_1_p3
  SUB_main main_1 (.S(RS2), .M(RS1), .out_3(main_1_out_3));  // open: Borrow
  AND_main main_2 (.R1(RS1), .R2(RS2), .Re(main_2_re));
  OR_main main_3 (.R1(RS1), .R2(RS2), .Re(main_3_re));
  SR_main main_4 (.N1(RS1), .Result(main_4_result));  // open: Overflow
  SL_main main_5 (.N1(RS1), .Result(main_5_result));  // open: Overflow
  SLT_main main_6 (.N1(RS1), .N2(RS2), .Bbit(main_6_bbit));
  assign Resultado = demultiplexer_1_out0 ? sumador_1_p3 : 16'bz;  // Controlled_Buffer controlled_buffer_1
  assign Resultado = demultiplexer_1_out1 ? main_1_out_3 : 16'bz;  // Controlled_Buffer controlled_buffer_2
  assign Resultado = demultiplexer_1_out2 ? main_2_re : 16'bz;  // Controlled_Buffer controlled_buffer_3
  assign Resultado = demultiplexer_1_out3 ? main_3_re : 16'bz;  // Controlled_Buffer controlled_buffer_4
  assign Resultado = demultiplexer_1_out4 ? main_4_result : 16'bz;  // Controlled_Buffer controlled_buffer_5
  assign Resultado = demultiplexer_1_out5 ? main_5_result : 16'bz;  // Controlled_Buffer controlled_buffer_6
  assign Bbit = demultiplexer_1_out6 ? main_6_bbit : 1'bz;  // Controlled_Buffer controlled_buffer_7
  EQ_main main_7 (.N1(RS1), .N2(RS2), .Branchbit(main_7_branchbit));
  assign Bbit = demultiplexer_1_out7 ? main_7_branchbit : 1'bz;  // Controlled_Buffer controlled_buffer_8
  Demultiplexer #(.select(4), .enable("false")) demultiplexer_1 (
    .out0(demultiplexer_1_out0), .out1(demultiplexer_1_out1), .out2(demultiplexer_1_out2),
    .out3(demultiplexer_1_out3), .out4(demultiplexer_1_out4), .out5(demultiplexer_1_out5),
    .out6(demultiplexer_1_out6), .out7(demultiplexer_1_out7), .in(1'b1), .sel(NEM));  // open: out8, out9, out10, out11, out12, out13, out14, out15
endmodule
