// Logisim project NEQ.circ as structural Verilog: 1 circuit, main circuit main
// NEQ
module main (
  input  [15:0] N1,
  input  [15:0] N2,
  output Branchbit
);

  wire or_1_out, or_2_out, or_3_out, or_4_out, or_5_out, or_6_out, or_7_out, or_8_out, or_9_out, or_10_out,
       or_11_out, or_12_out, or_13_out, or_14_out, or_15_out, or_16_out;

  or or_1 (or_1_out, N1[0], N2[0]);
  or or_2 (or_2_out, N1[1], N2[1]);
  or or_3 (or_3_out, N1[2], N2[2]);
  or or_4 (or_4_out, N1[3], N2[3]);
  or or_5 (or_5_out, N1[4], N2[4]);
  or or_6 (or_6_out, N1[5], N2[5]);
  or or_7 (or_7_out, N1[6], N2[6]);
  or or_8 (or_8_out, N1[7], N2[7]);
  or or_9 (or_9_out, N1[8], N2[8]);
  or or_10 (or_10_out, N1[9], N2[9]);
  or or_11 (or_11_out, N1[10], N2[10]);
  or or_12 (or_12_out, N1[11], N2[11]);
  or or_13 (or_13_out, N1[12], N2[12]);
  or or_14 (or_14_out, N1[13], N2[13]);
  or or_15 (or_15_out, N1[14], N2[14]);
  or or_16 (or_16_out, N1[15], N2[15]);
  or or_17 (Branchbit, or_1_out, or_2_out, or_3_out, or_4_out, or_5_out, or_6_out, or_7_out, or_8_out, or_9_out, or_10_out, or_11_out, or_12_out, or_13_out, or_14_out, or_15_out, or_16_out);
endmodule
