// Logisim project RL.circ as structural Verilog: 1 circuit, main circuit rl
module rl (
  input  [15:0] N1,
  output [15:0] Result,
  output Overflow
);


  assign Overflow = N1[15];
  assign Result = {N1[14:0], N1[15]};

  // Notes on the sheet:
  //   ROTACION A LA IZQUIERDA
endmodule
