// Logisim project RR.circ as structural Verilog: 1 circuit, main circuit rr
module rr (
  input  [15:0] N1,
  output [15:0] Result,
  output Overflow
);


  assign Overflow = N1[0];
  assign Result = {N1[0], N1[15:1]};

  // Notes on the sheet:
  //   ROTACION A  LA DERECHA
endmodule
