// Logisim project SLT.circ as structural Verilog: 1 circuit, main circuit main
module main (
  input  [15:0] N1,
  input  [15:0] N2,
  output Bbit
);

  Comparator #(.width(16)) comparator_1 (.a(N1), .b(N2), .lt(Bbit));  // open: gt, eq
endmodule
