// Logisim project SR.circ as structural Verilog: 1 circuit, main circuit main
module main (
  input  [15:0] N1,
  output Overflow,
  output [15:0] Result
);


  assign Overflow = N1[0];
  assign Result = {1'b0, N1[15:1]};
endmodule
