// Logisim project SUB.circ as structural Verilog: 1 circuit, main circuit restador
module restador (
  input  [15:0] M,
  input  [15:0] S,
  output [15:0] out_3,
  output Borrow
);

  wire and_1_out, and_2_out, and_3_out, and_4_out, and_5_out, and_6_out, and_7_out, and_8_out, and_9_out,
       and_10_out, and_11_out, and_12_out, and_13_out, and_14_out, and_15_out, and_16_out, and_17_out,
       and_18_out, and_19_out, and_20_out, and_21_out, and_22_out, and_23_out, and_24_out, and_25_out,
       and_26_out, and_27_out, and_28_out, and_29_out, and_30_out, and_31_out, and_32_out, B_2_out, B_3_out,
       B_4_out, B_5_out, B_6_out, B_7_out, B_8_out, B_9_out, B_10_out, B_11_out, B_12_out, B_13_out,
       B_14_out, B_15_out, B_out, not_1_out, not_2_out, not_3_out, not_4_out, not_5_out, not_6_out,
       not_7_out, not_8_out, not_9_out, not_10_out, not_11_out, not_12_out, not_13_out, not_14_out,
       not_15_out, not_16_out, not_17_out, not_18_out, not_19_out, not_20_out, not_21_out, not_22_out,
       not_23_out, not_24_out, not_25_out, not_26_out, not_27_out, not_28_out, not_29_out, not_30_out,
       not_31_out, not_32_out, xor_1_out, xor_2_out, xor_3_out, xor_4_out, xor_5_out, xor_6_out, xor_7_out,
       xor_8_out, xor_9_out, xor_10_out, xor_11_out, xor_12_out, xor_13_out, xor_14_out, xor_15_out,
       xor_16_out;

  not not_1 (not_1_out, M[12]);
  not not_2 (not_2_out, M[13]);
  not not_3 (not_3_out, M[14]);
  not not_4 (not_4_out, M[15]);
  not not_5 (not_5_out, M[4]);
  not not_6 (not_6_out, M[5]);
  not not_7 (not_7_out, M[6]);
  not not_8 (not_8_out, M[7]);
  not not_9 (not_9_out, M[8]);
  not not_10 (not_10_out, M[9]);
  not not_11 (not_11_out, M[10]);
  not not_12 (not_12_out, M[11]);
  not not_13 (not_13_out, M[0]);
  not not_14 (not_14_out, M[1]);
  not not_15 (not_15_out, M[2]);
  not not_16 (not_16_out, M[3]);
  xor xor_1 (xor_1_out, M[0], S[0]);
  and and_1 (and_1_out, not_13_out, S[0]);
  xor xor_2 (xor_2_out, M[1], S[1]);
  and and_2 (and_2_out, not_14_out, S[1]);
  xor xor_3 (xor_3_out, M[2], S[2]);
  and and_3 (and_3_out, not_15_out, S[2]);
  xor xor_4 (xor_4_out, M[3], S[3]);
  and and_4 (and_4_out, not_16_out, S[3]);
  xor xor_5 (xor_5_out, M[4], S[4]);
  and and_5 (and_5_out, not_5_out, S[4]);
  xor xor_6 (xor_6_out, M[5], S[5]);
  and and_6 (and_6_out, not_6_out, S[5]);
  xor xor_7 (xor_7_out, M[6], S[6]);
  and and_7 (and_7_out, not_7_out, S[6]);
  xor xor_8 (xor_8_out, M[7], S[7]);
  and and_8 (and_8_out, not_8_out, S[7]);
  xor xor_9 (xor_9_out, M[8], S[8]);
  and and_9 (and_9_out, not_9_out, S[8]);
  xor xor_10 (xor_10_out, M[9], S[9]);
  and and_10 (and_10_out, not_10_out, S[9]);
  xor xor_11 (xor_11_out, M[10], S[10]);
  and and_11 (and_11_out, not_11_out, S[10]);
  xor xor_12 (xor_12_out, M[11], S[11]);
  and and_12 (and_12_out, not_12_out, S[11]);
  xor xor_13 (xor_13_out, M[12], S[12]);
  and and_13 (and_13_out, not_1_out, S[12]);
  xor xor_14 (xor_14_out, M[13], S[13]);
  and and_14 (and_14_out, not_2_out, S[13]);
  xor xor_15 (xor_15_out, M[14], S[14]);
  and and_15 (and_15_out, not_3_out, S[14]);
  xor xor_16 (xor_16_out, M[15], S[15]);
  and and_16 (and_16_out, not_4_out, S[15]);
  xor T (out_3[0], xor_1_out, 1'b0);
  not not_17 (not_17_out, xor_1_out);
  and and_17 (and_17_out, not_17_out, 1'b0);
  xor xor_17 (out_3[1], xor_2_out, B_out);
  not not_18 (not_18_out, xor_2_out);
  and and_18 (and_18_out, not_18_out, B_out);
  xor xor_18 (out_3[2], xor_3_out, B_2_out);
  not not_19 (not_19_out, xor_3_out);
  and and_19 (and_19_out, not_19_out, B_2_out);
  xor xor_19 (out_3[3], xor_4_out, B_3_out);
  not not_20 (not_20_out, xor_4_out);
  and and_20 (and_20_out, not_20_out, B_3_out);
  xor xor_20 (out_3[4], xor_5_out, B_4_out);
  not not_21 (not_21_out, xor_5_out);
  and and_21 (and_21_out, not_21_out, B_4_out);
  xor xor_21 (out_3[5], xor_6_out, B_5_out);
  not not_22 (not_22_out, xor_6_out);
  and and_22 (and_22_out, not_22_out, B_5_out);
  xor xor_22 (out_3[6], xor_7_out, B_6_out);
  not not_23 (not_23_out, xor_7_out);
  and and_23 (and_23_out, not_23_out, B_6_out);
  xor xor_23 (out_3[7], xor_8_out, B_7_out);
  not not_24 (not_24_out, xor_8_out);
  and and_24 (and_24_out, not_24_out, B_7_out);
  xor xor_24 (out_3[8], xor_9_out, B_8_out);
  not not_25 (not_25_out, xor_9_out);
  and and_25 (and_25_out, not_25_out, B_8_out);
  xor xor_25 (out_3[9], xor_10_out, B_9_out);
  not not_26 (not_26_out, xor_10_out);
  and and_26 (and_26_out, not_26_out, B_9_out);
  xor xor_26 (out_3[10], xor_11_out, B_10_out);
  not not_27 (not_27_out, xor_11_out);
  and and_27 (and_27_out, not_27_out, B_10_out);
  xor xor_27 (out_3[11], xor_12_out, B_11_out);
  not not_28 (not_28_out, xor_12_out);
  and and_28 (and_28_out, not_28_out, B_11_out);
  xor xor_28 (out_3[12], xor_13_out, B_12_out);
  not not_29 (not_29_out, xor_13_out);
  and and_29 (and_29_out, not_29_out, B_12_out);
  xor xor_29 (out_3[13], xor_14_out, B_13_out);
  not not_30 (not_30_out, xor_14_out);
  and and_30 (and_30_out, not_30_out, B_13_out);
  xor xor_30 (out_3[14], xor_15_out, B_14_out);
  not not_31 (not_31_out, xor_15_out);
  and and_31 (and_31_out, not_31_out, B_14_out);
  xor xor_31 (out_3[15], xor_16_out, B_15_out);
  not not_32 (not_32_out, xor_16_out);
  and and_32 (and_32_out, not_32_out, B_15_out);
  or B (B_out, and_17_out, and_1_out);
  or B_2 (B_2_out, and_18_out, and_2_out);
  or B_3 (B_3_out, and_19_out, and_3_out);
  or B_4 (B_4_out, and_20_out, and_4_out);
  or B_5 (B_5_out, and_21_out, and_5_out);
  or B_6 (B_6_out, and_22_out, and_6_out);
  or B_7 (B_7_out, and_7_out, and_23_out);
  or B_8 (B_8_out, and_8_out, and_24_out);
  or B_9 (B_9_out, and_9_out, and_25_out);
  or B_10 (B_10_out, and_10_out, and_26_out);
  or B_11 (B_11_out, and_11_out, and_27_out);
  or B_12 (B_12_out, and_12_out, and_28_out);
  or B_13 (B_13_out, and_13_out, and_29_out);
  or B_14 (B_14_out, and_14_out, and_30_out);
  or B_15 (B_15_out, and_15_out, and_31_out);
  or B_16 (Borrow, and_16_out, and_32_out);
endmodule
