// Logisim project XOR.circ as structural Verilog: 1 circuit, main circuit xor
module \xor  (
  input  [15:0] in_1,
  input  [15:0] in_2,
  output [15:0] Resp
);

  xor xor_1 (Resp[0], in_1[0], in_2[0]);
  xor xor_2 (Resp[1], in_1[1], in_2[1]);
  xor xor_3 (Resp[2], in_1[2], in_2[2]);
  xor xor_4 (Resp[3], in_1[3], in_2[3]);
  xor xor_5 (Resp[4], in_1[4], in_2[4]);
  xor xor_6 (Resp[5], in_1[5], in_2[5]);
  xor xor_7 (Resp[6], in_1[6], in_2[6]);
  xor xor_8 (Resp[7], in_1[7], in_2[7]);
  xor xor_9 (Resp[8], in_1[8], in_2[8]);
  xor xor_10 (Resp[9], in_1[9], in_2[9]);
  xor xor_11 (Resp[10], in_1[10], in_2[10]);
  xor xor_12 (Resp[11], in_1[11], in_2[11]);
  xor xor_13 (Resp[12], in_1[12], in_2[12]);
  xor xor_14 (Resp[13], in_1[13], in_2[13]);
  xor xor_15 (Resp[14], in_1[14], in_2[14]);
  xor xor_16 (Resp[15], in_1[15], in_2[15]);

  // Notes on the sheet:
  //   R1
  //   R2
  //   CIRCUITO XOR
endmodule
