// Logisim project MEM.circ as structural Verilog: 1 circuit, main circuit main
module main (
  input  [3:0] NEM,
  input  [3:0] RF1,
  input  [3:0] RF2,
  input  [15:0] Dir_RF1,
  input  [15:0] Guar_RF2,
  input  [15:0] Redest_RD,
  output [15:0] Resultado,
  output [15:0] Address_RF1,
  output [15:0] Store_RF2,
  output ActR
);

  wire demultiplexer_1_out8, demultiplexer_1_out9, demultiplexer_1_out10, demultiplexer_1_out11;
  wire [15:0] main_1_result, main_2_result;

  Demultiplexer #(.select(4), .disabled(0), .enable("false")) demultiplexer_1 (
    .out8(demultiplexer_1_out8), .out9(demultiplexer_1_out9), .out10(demultiplexer_1_out10),
    .out11(demultiplexer_1_out11), .in(1'b1), .sel(NEM));  // open: out0, out1, out2, out3, out4, out5, out6, out7, out12, out13, out14, out15
  LI_main main_1 (.Rdc1(RF1), .Rdc2(RF2), .Result(main_1_result));
  assign Resultado = demultiplexer_1_out10 ? main_1_result : 16'bz;  // Controlled_Buffer controlled_buffer_1
  LUI_main main_2 (.Rdc1(RF1), .Rdc2(RF2), .Result(main_2_result));
  assign Resultado = demultiplexer_1_out11 ? main_2_result : 16'bz;  // Controlled_Buffer controlled_buffer_2
  assign Address_RF1 = demultiplexer_1_out8 ? Dir_RF1 : 16'bz;  // Controlled_Buffer controlled_buffer_3
  assign ActR = demultiplexer_1_out8 ? 1'b1 : 1'bz;  // Controlled_Buffer controlled_buffer_4
  assign Store_RF2 = demultiplexer_1_out8 ? Guar_RF2 : 16'bz;  // Controlled_Buffer controlled_buffer_5
  assign ActR = demultiplexer_1_out9 ? 1'b0 : 1'bz;  // Controlled_Buffer controlled_buffer_6
  assign Address_RF1 = demultiplexer_1_out9 ? Dir_RF1 : 16'bz;  // Controlled_Buffer controlled_buffer_7
  assign Resultado = demultiplexer_1_out9 ? Redest_RD : 16'bz;  // Controlled_Buffer controlled_buffer_8
endmodule
