// Logisim project LUI.circ as structural Verilog: 1 circuit, main circuit lui
module lui (
  input  [3:0] Rdc1,
  input  [15:0] Rlow,
  input  [3:0] Rdc2,
  output [15:0] Result
);


  assign Result = {Rdc1, Rdc2, Rlow[7:0]};

  // Notes on the sheet:
  //   ALMACENAMIENTO PARTE ALTA
endmodule
