// Logisim project SWAP.circ as structural Verilog: 1 circuit, main circuit swp
module swp (
  input  [15:0] RN1,
  output [15:0] Result
);


  assign Result = {RN1[7:0], RN1[15:8]};

  // Notes on the sheet:
  //   INTERCAMBIO BAJA <-> ALTA
endmodule
