// Logisim project REG's.circ as structural Verilog: 1 circuit, main circuit main
module main (
  input  [15:0] in_1,
  input  in_2,
  input  [6:0] in_3,
  input  in_4,
  input  in_5,
  input  [3:0] in_6,
  input  [3:0] in_7,
  input  [3:0] in_8,
  output [6:0] out_9,
  output out_10,
  output out_11,
  output [15:0] out_12,
  output [15:0] out_13
);

  wire and_1_out, demultiplexer_1_out0, demultiplexer_1_out1, demultiplexer_1_out2, demultiplexer_1_out3,
       demultiplexer_1_out4, demultiplexer_1_out5, demultiplexer_1_out6, demultiplexer_1_out7,
       demultiplexer_1_out8, demultiplexer_1_out9, demultiplexer_1_out10, demultiplexer_1_out11,
       demultiplexer_1_out12, demultiplexer_1_out13, demultiplexer_1_out14, demultiplexer_1_out15, not_1_out;
  wire [15:0] multiplexer_2_out, register_2_q, register_3_q, register_4_q, register_5_q, register_6_q,
       register_7_q, register_8_q, register_9_q, register_10_q, register_11_q, register_12_q, register_13_q,
       register_14_q, register_15_q, register_16_q;
  wire [15:9] register_1_q;

  Demultiplexer #(.select(4), .enable("false")) demultiplexer_1 (
    .out0(demultiplexer_1_out0), .out1(demultiplexer_1_out1), .out2(demultiplexer_1_out2),
    .out3(demultiplexer_1_out3), .out4(demultiplexer_1_out4), .out5(demultiplexer_1_out5),
    .out6(demultiplexer_1_out6), .out7(demultiplexer_1_out7), .out8(demultiplexer_1_out8),
    .out9(demultiplexer_1_out9), .out10(demultiplexer_1_out10), .out11(demultiplexer_1_out11),
    .out12(demultiplexer_1_out12), .out13(demultiplexer_1_out13), .out14(demultiplexer_1_out14),
    .out15(demultiplexer_1_out15), .in(1'b1), .sel(in_6));
  Multiplexer #(.select(4), .width(16), .enable("false")) multiplexer_1 (
    .in0({register_1_q, out_11, out_10, out_9}), .in1(register_3_q), .in2(register_5_q), .in3(register_7_q),
    .in4(register_9_q), .in5(register_11_q), .in6(register_13_q), .in7(register_15_q), .in8(register_16_q),
    .in9(register_14_q), .in10(register_12_q), .in11(register_10_q), .in12(register_8_q),
    .in13(register_6_q), .in14(register_4_q), .in15(register_2_q), .out(out_12), .sel(in_8));
  Register #(.width(16)) register_1 (
    .D(multiplexer_2_out), .en(demultiplexer_1_out0), .Q({register_1_q, out_11, out_10, out_9}), .clk(in_2),
    .clr(in_5));
  Register #(.width(16)) register_2 (.D(in_1), .en(demultiplexer_1_out15), .Q(register_2_q), .clk(in_2), .clr(in_5));
  Register #(.width(16)) register_3 (.D(in_1), .en(demultiplexer_1_out1), .Q(register_3_q), .clk(in_2), .clr(in_5));
  Register #(.width(16)) register_4 (.D(in_1), .en(demultiplexer_1_out14), .Q(register_4_q), .clk(in_2), .clr(in_5));
  Register #(.width(16)) register_5 (.D(in_1), .en(demultiplexer_1_out2), .Q(register_5_q), .clk(in_2), .clr(in_5));
  Register #(.width(16)) register_6 (.D(in_1), .en(demultiplexer_1_out13), .Q(register_6_q), .clk(in_2), .clr(in_5));
  Register #(.width(16)) register_7 (.D(in_1), .en(demultiplexer_1_out3), .Q(register_7_q), .clk(in_2), .clr(in_5));
  Register #(.width(16)) register_8 (.D(in_1), .en(demultiplexer_1_out12), .Q(register_8_q), .clk(in_2), .clr(in_5));
  Register #(.width(16)) register_9 (.D(in_1), .en(demultiplexer_1_out4), .Q(register_9_q), .clk(in_2), .clr(in_5));
  Register #(.width(16)) register_10 (.D(in_1), .en(demultiplexer_1_out11), .Q(register_10_q), .clk(in_2), .clr(in_5));
  Register #(.width(16)) register_11 (.D(in_1), .en(demultiplexer_1_out5), .Q(register_11_q), .clk(in_2), .clr(in_5));
  Register #(.width(16)) register_12 (.D(in_1), .en(demultiplexer_1_out10), .Q(register_12_q), .clk(in_2), .clr(in_5));
  Register #(.width(16)) register_13 (.D(in_1), .en(demultiplexer_1_out6), .Q(register_13_q), .clk(in_2), .clr(in_5));
  Register #(.width(16)) register_14 (.D(in_1), .en(demultiplexer_1_out9), .Q(register_14_q), .clk(in_2), .clr(in_5));
  Register #(.width(16)) register_15 (.D(in_1), .en(demultiplexer_1_out7), .Q(register_15_q), .clk(in_2), .clr(in_5));
  Register #(.width(16)) register_16 (.D(in_1), .en(demultiplexer_1_out8), .Q(register_16_q), .clk(in_2), .clr(in_5));
  Multiplexer #(.width(16), .enable("false")) multiplexer_2 (
    .in0(in_1), .in1({{7{1'b0}}, {2{in_4}}, in_3}), .out(multiplexer_2_out), .sel(and_1_out));
  and and_1 (and_1_out, not_1_out, out_11);
  not not_1 (not_1_out, in_4);
  Multiplexer #(.select(4), .width(16), .enable("false")) multiplexer_3 (
    .in0({register_1_q, out_11, out_10, out_9}), .in1(register_3_q), .in2(register_5_q), .in3(register_7_q),
    .in4(register_9_q), .in5(register_11_q), .in6(register_13_q), .in7(register_15_q), .in8(register_16_q),
    .in9(register_14_q), .in10(register_12_q), .in11(register_10_q), .in12(register_8_q),
    .in13(register_6_q), .in14(register_4_q), .in15(register_2_q), .out(out_13), .sel(in_7));
endmodule
